// Logisim project Lobo Guará.circ as structural Verilog: 3 circuits, main circuit main
module main (
  input  in_1
);

  wire clock_1_out;
  wire [7:0] adder_1_out, PC_q;

  Register PC (.D(adder_1_out), .en(1'b1), .clk(clock_1_out), .Q(PC_q), .clr(in_1));
  Clock clock_1 (.out(clock_1_out));
  Adder adder_1 (.a(8'h1), .b(PC_q), .out(adder_1_out));  // open: cin, cout
  ROM rom_1 (.addr(PC_q));  // open: data
  bancoDeRegistradores bancoderegistradores_1 ();  // open: ReadRegister1, ReadRegister2, WriteData, WriteRegister, RegWrite, CLOCK, CLEAR, ReadData1, ReadData2
  ULA ula_1 ();  // open: A, Funcao, B, in_4, Resultado, Igual, out_7
endmodule

module bancoDeRegistradores (
  input  [1:0] ReadRegister1,
  input  [1:0] ReadRegister2,
  input  [3:0] WriteData,
  input  [1:0] WriteRegister,
  input  RegWrite,
  input  CLOCK,
  input  CLEAR,
  output [3:0] ReadData1,
  output [3:0] ReadData2
);

  wire WE0, WE1, WE2, WE3;
  wire [3:0] Reg0In, Reg0Out, Reg1In, Reg1Out, Reg2In, Reg2Out, Reg3In, Reg3Out;

  Demultiplexer #(.select(2), .width(4), .disabled("Z")) demultiplexer_1 (
    .out0(Reg0In), .out1(Reg1In), .out2(Reg2In), .out3(Reg3In), .in(WriteData), .sel(WriteRegister));  // open: en
  Demultiplexer #(.select(2), .disabled("Z")) demultiplexer_2 (
    .out0(WE0), .out1(WE1), .out2(WE2), .out3(WE3), .in(RegWrite), .sel(WriteRegister));  // open: en
  Register #(.width(4)) Reg0 (.D(Reg0In), .en(WE0), .clk(CLOCK), .Q(Reg0Out), .clr(CLEAR));
  Register #(.width(4)) Reg1 (.D(Reg1In), .en(WE1), .clk(CLOCK), .Q(Reg1Out), .clr(CLEAR));
  Register #(.width(4)) Reg2 (.D(Reg2In), .en(WE2), .clk(CLOCK), .Q(Reg2Out), .clr(CLEAR));
  Register #(.width(4)) Reg3 (.D(Reg3In), .en(WE3), .clk(CLOCK), .Q(Reg3Out), .clr(CLEAR));
  Multiplexer #(.select(2), .width(4), .disabled("Z"), .enable("false")) multiplexer_1 (
    .in0(Reg0Out), .in1(Reg1Out), .in2(Reg2Out), .in3(Reg3Out), .out(ReadData1), .sel(ReadRegister1));
  Multiplexer #(.select(2), .width(4), .disabled("Z"), .enable("false")) multiplexer_2 (
    .in0(Reg0Out), .in1(Reg1Out), .in2(Reg2Out), .in3(Reg3Out), .out(ReadData2), .sel(ReadRegister2));
endmodule

module ULA (
  input  [7:0] A,
  input  [3:0] Funcao,
  input  [7:0] B,
  input  [7:0] in_4,
  output [7:0] Resultado,
  output Igual,
  output [7:0] out_7
);

  wire comparator_1_eq;
  wire [2:0] bit_extender_1_out, bit_extender_2_out;
  wire [7:0] AAddIn, AAndIn, ABrziIn, ABrzrIn, AddOut, AIdIn, AJiIn, AJrIn, AMovhIn, AMovlIn, AndOut, AOrIn,
       ASlrIn, ASrrIn, AStIn, ASubIn, BAddIn, BAndIn, BBrziIn, BBrzrIn, BIdIn, BJiIn, BJrIn, BMovhIn,
       BMovlIn, BMovrIn, BNotIn, BOrIn, BrziOut, BrzrOut, BSlrIn, BSrrIn, BStIn, BSubIn, IdOut, JiOut, JrOut,
       MovhOut, MovlOut, NotOut, OrOut, SlrOut, SrrOut, StOut, SubOut;

  Demultiplexer #(.select(4), .width(8), .enable("false")) demultiplexer_1 (
    .out0(ABrzrIn), .out1(ABrziIn), .out2(AJrIn), .out3(AJiIn), .out4(AIdIn), .out5(AStIn), .out7(AMovhIn),
    .out8(AMovlIn), .out9(AAddIn), .out10(ASubIn), .out11(AAndIn), .out12(AOrIn), .out14(ASlrIn),
    .out15(ASrrIn), .in(A), .sel(Funcao));  // open: out6, out13
  Demultiplexer #(.select(4), .width(8), .enable("false")) demultiplexer_2 (
    .out0(BBrzrIn), .out1(BBrziIn), .out2(BJrIn), .out3(BJiIn), .out4(BIdIn), .out5(BStIn), .out6(BMovrIn),
    .out7(BMovhIn), .out8(BMovlIn), .out9(BAddIn), .out10(BSubIn), .out11(BAndIn), .out12(BOrIn),
    .out13(BNotIn), .out14(BSlrIn), .out15(BSrrIn), .in(B), .sel(Funcao));
  Comparator comparator_1 (.a(ABrzrIn), .b(in_4), .eq(comparator_1_eq));  // open: gt, lt
  Multiplexer #(.width(8), .enable("false")) multiplexer_1 (
    .in1(BBrzrIn), .out(out_7), .sel(comparator_1_eq));  // open: in0
  assign NotOut = ~BNotIn;  // NOT_Gate not_1, 8 bits wide
  assign OrOut = AOrIn | BOrIn;  // OR_Gate or_1, 8 bits wide
  assign AndOut = AAndIn & BAndIn;  // AND_Gate and_1, 8 bits wide
  Subtractor subtractor_1 (.a(ASubIn), .b(BSubIn), .out(SubOut));  // open: bin, bout
  Adder adder_1 (.a(AAddIn), .b(BAddIn), .out(AddOut));  // open: cin, cout
  Bit_Extender #(.out_width(3)) bit_extender_1 (.in(BSlrIn), .out(bit_extender_1_out));
  Bit_Extender #(.out_width(3)) bit_extender_2 (.in(BSrrIn), .out(bit_extender_2_out));
  Multiplexer #(.select(4), .width(8), .enable("false")) multiplexer_2 (
    .in0(BrzrOut), .in1(BrziOut), .in2(JrOut), .in3(JiOut), .in4(IdOut), .in5(StOut), .in6(BMovrIn),
    .in7(MovhOut), .in8(MovlOut), .in9(AddOut), .in10(SubOut), .in11(AndOut), .in12(OrOut), .in13(NotOut),
    .in14(SlrOut), .in15(SrrOut), .out(Resultado), .sel(Funcao));
  Shifter shifter_1 (.in(ASlrIn), .\dist (bit_extender_1_out), .out(SlrOut));
  Shifter #(.shift("lr")) shifter_2 (.in(ASrrIn), .\dist (bit_extender_2_out), .out(SrrOut));

  // Other names for the same wires on the sheet: MovrOut[7:0] = BMovrIn
endmodule
